# Fritzing sketch Example_Analog_Input (saved by Fritzing 0.7.4b)
breadboards: 1

parts:
  Launchpad1 = TI Launchpad MSP430G2
  R1 = Trimmer Potentiometer [maximum_resistance=10kΩ package=THT]

nets:
  N1: Launchpad1.p7, R1.wiper
  N2: Launchpad1.p1, R1.leg1
  N3: Launchpad1.p20, R1.leg2
