# Fritzing sketch Example_PWM_Servo (saved by Fritzing 0.7.4b)
breadboards: 1

parts:
  Launchpad1 = TI Launchpad MSP430G2
  J1 = Basic Servo
  VCC1 = 4 x AAA Battery Mount

nets:
  N1: Launchpad1.p10, J1.pulse
  N2: Launchpad1.p20, J1.gnd, VCC1.-
  N3: J1.vcc, VCC1.+
